// Logisim project rg8.circ as structural Verilog
module demi_add (
  input  a,
  input  b,
  output s,
  output r
);

  xor xor_1 (s, a, b);
  and and_1 (r, a, b);
endmodule

module add_full (
  input  a,
  input  b,
  input  cin,
  output s,
  output cout
);

  wire demi_add_1_r, demi_add_1_s, demi_add_2_r;

  demi_add demi_add_1 (.a(a), .b(b), .s(demi_add_1_s), .r(demi_add_1_r));
  demi_add demi_add_2 (.a(demi_add_1_s), .b(cin), .s(s), .r(demi_add_2_r));
  or or_1 (cout, demi_add_2_r, demi_add_1_r);
endmodule
